// Logisim project will this work 2.circ as structural Verilog: 2 circuits, main circuit main
// CB
module main (
  output out_1
);

  wire A, B, CA_out, clock_1_out, clock_2_out, d_ff_1_q, d_ff_3_q, G, GS, not_1_out, or_1_out, Push, R, RS,
       undriven, Y, YS;
  wire [3:0] X;

  Hex_Digit_Display hex_digit_display_1 (.value(X));  // open: dp
  LED led_1 (.in(out_1));
  LED led_2 (.in(out_1));
  LED Barrier_2 (.in(A));
  LED led_3 (.in(RS));
  LED led_4 (.in(YS));
  LED led_5 (.in(GS));
  LED Barrier1 (.in(A));
  LED led_6 (.in(R));
  LED led_7 (.in(Y));
  LED led_8 (.in(G));
  Button button_1 (.out(Push));
  or or_1 (or_1_out, Push, 1'b0);
  LED led_9 (.in(A));
  Clock CA (.out(CA_out));
  Traffic_Light traffic_light_1 (.push_button(A), .R(R), .Y(Y), .G(G), .RS(RS), .YS(YS), .GS(GS));
  not not_1 (not_1_out, A);
  Clock clock_1 (.out(clock_1_out));
  // Probe on d_ff_1_q
  D_Flip_Flop d_ff_1 (.clk(CA_out), .D(or_1_out), .Q(d_ff_1_q));  // open: Qn, preset, en, reset
  Counter #(.width(4), .max('hf)) counter_1 (
    .count(undriven), .Q(X), .clk(clock_1_out), .clr(not_1_out));  // open: load, D, carry
  D_Flip_Flop d_ff_2 (.clk(d_ff_1_q), .D(or_1_out), .Q(A), .reset(B));  // open: Qn, preset, en
  Hex_Digit_Display hex_digit_display_2 (.value(X));  // open: dp
  // Probe on X
  and and_1 (B, X[0], X[1], X[2], X[3]);
  Clock #(.highDuration(4), .lowDuration(2)) clock_2 (.out(clock_2_out));
  D_Flip_Flop d_ff_3 (.clk(clock_2_out), .D(A), .Q(d_ff_3_q));  // open: Qn, preset, en, reset
  and and_2 (out_1, d_ff_3_q, clock_2_out);
  LED led_10 (.in(out_1));

  // Other names for the same wires on the sheet: Alert_Alarm = out_1; barrier = A

  // Notes on the sheet:
  //   TRAIN  ALERT
  //   P1
  //   P2
  //   Barriers closed
  //   Train detection
  //   Traffic Lights
  //   sensor
  //   GATE CLOSE
  //   Timer 
endmodule

module Traffic_Light (
  input  push_button,
  output R,
  output Y,
  output G,
  output RS,
  output YS,
  output GS
);

  wire clock_1_out, clock_2_out;
  wire [2:0] counter_1_q, counter_2_q, rom_1_data, rom_2_data;

  Clock clock_1 (.out(clock_1_out));
  Clock clock_2 (.out(clock_2_out));
  Counter #(.width(3), .max('h7)) counter_1 (
    .count(clock_1_out), .Q(counter_1_q), .clk(clock_1_out));  // open: load, D, carry, clr
  Counter #(.width(3), .max('h7)) counter_2 (
    .count(clock_2_out), .Q(counter_2_q), .clk(clock_2_out));  // open: load, D, carry, clr
  ROM #(.addrWidth(3), .dataWidth(3)) rom_1 (.addr(counter_1_q), .data(rom_1_data));  // open: sel
  ROM #(.addrWidth(3), .dataWidth(3)) rom_2 (.addr(counter_2_q), .data(rom_2_data));  // open: sel
  Multiplexer #(.enable("false")) multiplexer_1 (.in0(rom_1_data[0]), .in1(1'b1), .out(R), .sel(push_button));
  Multiplexer #(.enable("false")) multiplexer_2 (.in0(rom_1_data[1]), .in1(1'b0), .out(Y), .sel(push_button));
  Multiplexer #(.enable("false")) multiplexer_3 (.in0(rom_1_data[2]), .in1(1'b0), .out(G), .sel(push_button));
  Multiplexer #(.enable("false")) multiplexer_4 (.in0(rom_2_data[0]), .in1(1'b1), .out(RS), .sel(push_button));
  Multiplexer #(.enable("false")) multiplexer_5 (.in0(rom_2_data[1]), .in1(1'b0), .out(YS), .sel(push_button));
  Multiplexer #(.enable("false")) multiplexer_6 (.in0(rom_2_data[2]), .in1(1'b0), .out(GS), .sel(push_button));
  LED led_1 (.in(R));
  LED led_2 (.in(Y));
  LED led_3 (.in(G));
  LED led_4 (.in(RS));
  LED led_5 (.in(YS));
  LED led_6 (.in(GS));

  // Notes on the sheet:
  //   contents of rom_1 (hex, n*v repeats v):
  //   1 3 2 4 0 4 2 1
  //   contents of rom_2 (hex, n*v repeats v):
  //   4 2 1 1 0 1 3 4
endmodule
